# Fritzing sketch LCD_using_74HC595_and_SPI (saved by Fritzing 0.6.5b)
breadboards: 1

parts:
  Arduino1 = Arduino
  U1 = 74HC595 [package="DIP16 [THT]"]
  LCD1 = LCD screen
  R1 = Rotary Potentiometer (Large) [maximum_resistance=10kΩ package=THT]

nets:
  GND: Arduino1.GND, U1.GND, U1.OE, LCD1.VSS, R1.leg1
  N1: Arduino1.D13, U1.SH_CP
  N2: Arduino1.D11, U1.DS
  N3: Arduino1.D10, U1.ST_CP
  +5V: Arduino1.+5V, U1.MR, U1.VCC, LCD1.VDD, R1.leg2
  N4: U1.Q1, LCD1.RS
  N5: U1.Q3, LCD1.E
  N6: U1.Q4, LCD1.DB4
  N7: U1.Q5, LCD1.DB5
  N8: U1.Q6, LCD1.DB6
  N9: U1.Q7, LCD1.DB7
  N10: LCD1.V0, R1.wiper
